// Logisim project Practica4.circ as structural Verilog
module XOR (
  input  P,
  input  Q,
  output P_XOR_Q
);

  wire and_1_out, and_2_out, not_1_out, not_2_out;

  not not_1 (not_1_out, P);
  not not_2 (not_2_out, Q);
  and and_1 (and_1_out, not_1_out, Q);
  and and_2 (and_2_out, P, not_2_out);
  or or_1 (P_XOR_Q, and_1_out, and_2_out);

  // Notes on the sheet:
  //   Compuerta XOR
endmodule

// ALU
module ALU_1_bit_suma (
  input  Ci,
  input  [1:0] Op,
  input  A,
  input  B,
  output S,
  output Ci_1
);

  wire and_1_out, and_2_out, and_3_out, or_1_out, xor_1_p_xor_q, xor_2_p_xor_q;

  and and_1 (and_1_out, B, A);
  and and_2 (and_2_out, A, B);
  or or_1 (or_1_out, A, B);
  XOR xor_1 (.P(A), .Q(B), .P_XOR_Q(xor_1_p_xor_q));
  and and_3 (and_3_out, Ci, xor_1_p_xor_q);
  or or_2 (Ci_1, and_1_out, and_3_out);
  XOR xor_2 (.P(Ci), .Q(xor_1_p_xor_q), .P_XOR_Q(xor_2_p_xor_q));
  Multiplexer #(.select(2)) multiplexer_1 (
    .in0(and_2_out), .in1(or_1_out), .in2(xor_2_p_xor_q), .out(S), .sel(Op));  // open: in3, en

  // Notes on the sheet:
  //   ALU de 1 bit
endmodule

module ALU_8_bits_suma (
  input  Ci,
  input  [1:0] in_2,
  input  A0,
  input  B0,
  input  A1,
  input  B1,
  input  A2,
  input  B2,
  input  A3,
  input  B3,
  input  A4,
  input  B4,
  input  A5,
  input  B5,
  input  A6,
  input  B6,
  input  A7,
  input  B7,
  output S0,
  output S1,
  output S2,
  output S3,
  output S4,
  output S5,
  output S6,
  output S2_2,
  output Desbordamiento,
  output S7
);

  wire alu_1_bit_suma_1_ci_1, alu_1_bit_suma_2_ci_1, alu_1_bit_suma_3_ci_1, alu_1_bit_suma_4_ci_1,
       alu_1_bit_suma_5_ci_1, alu_1_bit_suma_6_ci_1, alu_1_bit_suma_7_ci_1;

  ALU_1_bit_suma alu_1_bit_suma_1 (.A(A0), .B(B0), .S(S0), .Ci(Ci), .Op(in_2), .Ci_1(alu_1_bit_suma_1_ci_1));
  ALU_1_bit_suma alu_1_bit_suma_2 (
    .A(A1), .B(B1), .S(S1), .Ci(alu_1_bit_suma_1_ci_1), .Op(in_2), .Ci_1(alu_1_bit_suma_2_ci_1));
  ALU_1_bit_suma alu_1_bit_suma_3 (
    .A(A2), .B(B2), .S(S2), .Ci(alu_1_bit_suma_2_ci_1), .Op(in_2), .Ci_1(alu_1_bit_suma_3_ci_1));
  ALU_1_bit_suma alu_1_bit_suma_4 (
    .A(A3), .B(B3), .S(S3), .Ci(alu_1_bit_suma_3_ci_1), .Op(in_2), .Ci_1(alu_1_bit_suma_4_ci_1));
  ALU_1_bit_suma alu_1_bit_suma_5 (
    .A(A4), .B(B4), .S(S4), .Ci(alu_1_bit_suma_4_ci_1), .Op(in_2), .Ci_1(alu_1_bit_suma_5_ci_1));
  ALU_1_bit_suma alu_1_bit_suma_6 (
    .A(A5), .B(B5), .S(S5), .Ci(alu_1_bit_suma_5_ci_1), .Op(in_2), .Ci_1(alu_1_bit_suma_6_ci_1));
  ALU_1_bit_suma alu_1_bit_suma_7 (
    .A(A6), .B(B6), .S(S6), .Ci(alu_1_bit_suma_6_ci_1), .Op(in_2), .Ci_1(alu_1_bit_suma_7_ci_1));
  ALU_1_bit_suma alu_1_bit_suma_8 (
    .A(A7), .B(B7), .S(S2_2), .Ci(alu_1_bit_suma_7_ci_1), .Op(in_2), .Ci_1(Desbordamiento));

  // Notes on the sheet:
  //   ALU de 8 bits
endmodule

module ALU_1_bit_resta (
  input  Ci,
  input  [1:0] Op,
  input  A,
  input  B,
  output S,
  output Ci_1
);

  wire and_1_out, and_2_out, and_3_out, not_1_out, or_2_out, xor_1_p_xor_q, xor_2_p_xor_q, xor_3_p_xor_q,
       xor_4_p_xor_q;

  not not_1 (not_1_out, B);
  XOR xor_1 (.P(A), .Q(B), .P_XOR_Q(xor_1_p_xor_q));
  and and_1 (and_1_out, B, A);
  or or_1 (Ci_1, and_1_out, and_3_out);
  and and_2 (and_2_out, A, B);
  or or_2 (or_2_out, A, B);
  XOR xor_2 (.P(Ci), .Q(xor_1_p_xor_q), .P_XOR_Q(xor_2_p_xor_q));
  and and_3 (and_3_out, Ci, xor_1_p_xor_q);
  Multiplexer #(.select(2)) multiplexer_1 (
    .in0(and_2_out), .in1(or_2_out), .in2(xor_2_p_xor_q), .in3(xor_3_p_xor_q), .out(S), .sel(Op));  // open: en
  XOR xor_3 (.P(xor_4_p_xor_q), .Q(1'b0), .P_XOR_Q(xor_3_p_xor_q));
  XOR xor_4 (.P(1'b1), .Q(not_1_out), .P_XOR_Q(xor_4_p_xor_q));

  // Notes on the sheet:
  //   ALU de 1 bit
endmodule
